// Logisim project arithmetic.circ as structural Verilog: 1 circuit, main circuit main
module main (
  input  in_1,
  input  in_2,
  input  in_3,
  input  in_4,
  input  in_5,
  input  in_6,
  input  in_7,
  input  in_8,
  input  in_9,
  input  in_10,
  output out_11,
  output out_12,
  output out_13,
  output out_14,
  output out_15,
  output out_16,
  output out_17,
  output out_18
);

  wire and_2_out, and_3_out, and_4_out, and_6_out, buffer_1_out, buffer_2_out, buffer_3_out, xor_1_out,
       xor_5_out;

  xor xor_1 (xor_1_out, in_5, in_7);
  xor xor_2 (out_11, in_1, in_4);
  and and_1 (out_13, in_1, in_4);
  and and_2 (and_2_out, in_9, xor_1_out);
  and and_3 (and_3_out, in_7, in_5);
  xor xor_3 (out_15, xor_1_out, in_9);
  or or_1 (out_17, and_2_out, and_3_out);
  buf buffer_1 (buffer_1_out, in_2);
  buf buffer_2 (buffer_2_out, in_6);
  xor xor_4 (out_12, in_2, in_3);
  xor xor_5 (xor_5_out, in_6, in_8);
  and and_4 (and_4_out, buffer_2_out, in_8);
  and and_5 (out_14, buffer_1_out, in_3);
  buf buffer_3 (buffer_3_out, xor_5_out);
  xor xor_6 (out_16, xor_5_out, in_10);
  and and_6 (and_6_out, buffer_3_out, in_10);
  or or_2 (out_18, and_6_out, and_4_out);

  // Notes on the sheet:
  //   HALF ADDER
  //   FULL ADDER
  //   HALF SUBTRACTOR
  //   FULL SUBTRACTOR
endmodule
