// Logisim project demultiplexers.circ as structural Verilog: 1 circuit, main circuit main
module main (
  input  in_1,
  input  in_2,
  input  in_3,
  input  in_4,
  input  in_5,
  output out_6,
  output out_7,
  output out_8,
  output out_9,
  output out_10,
  output out_11
);

  wire not_1_out, not_2_out, not_3_out;

  not not_1 (not_1_out, in_4);
  not not_2 (not_2_out, in_5);
  not not_3 (not_3_out, in_1);
  and and_1 (out_6, not_3_out, in_2);
  and and_2 (out_7, in_2, in_1);
  and and_3 (out_8, in_4, in_5, in_3);
  and and_4 (out_9, in_4, not_2_out, in_3);
  and and_5 (out_10, not_1_out, in_5, in_3);
  and and_6 (out_11, not_2_out, not_1_out, in_3);

  // Notes on the sheet:
  //   1*4 demultiplexer
  //   1*2 demultiplexer
  //   DEMULTIPLEXERS
endmodule
