// Logisim project logicgates.circ as structural Verilog: 1 circuit, main circuit main
module main (
  input  in_1,
  input  in_2,
  input  in_3,
  input  in_4,
  input  in_5,
  input  in_6,
  input  in_7,
  input  in_8,
  input  in_9,
  input  in_10,
  input  _3__NOT,
  input  in_12,
  input  in_13,
  input  in_14,
  input  in_15,
  input  in_16,
  input  in_17
);

  wire and_1_out, and_2_out, nand_1_out, nor_1_out, not_1_out, not_2_out, not_3_out, or_1_out, or_2_out,
       xnor_1_out, xor_1_out;

  or or_1 (or_1_out, in_1, in_3);
  and and_1 (and_1_out, in_6, in_8);
  not not_1 (not_1_out, _3__NOT);
  LED led_1 (.in(or_1_out));
  LED led_2 (.in(and_1_out));
  LED led_3 (.in(not_1_out));
  xor xor_1 (xor_1_out, in_14, in_15);
  xnor xnor_1 (xnor_1_out, in_16, in_17);
  LED led_4 (.in(xor_1_out));
  LED led_5 (.in(xnor_1_out));
  or or_2 (or_2_out, in_2, in_4);
  nor nor_1 (nor_1_out, in_5, in_7);
  and and_2 (and_2_out, in_9, in_10);
  nand nand_1 (nand_1_out, in_12, in_13);
  not not_2 (not_2_out, or_2_out);
  not not_3 (not_3_out, and_2_out);
  LED led_6 (.in(not_2_out));
  LED led_7 (.in(nor_1_out));
  LED led_8 (.in(not_3_out));
  LED led_9 (.in(nand_1_out));

  // Notes on the sheet:
  //   1) OR
  //   2) AND
  //   1) Ex -OR
  //   2) Ex-NOR
  //   BASIC GATES
  //   SPECIAL GATES
  //   LOGIC GATES
  //   1) NOR
  //   2) NAND
  //   UNIVERSAL GATES
endmodule
